# Fritzing sketch ToyKitchenWiring (saved by Fritzing 0.8.5b)
circuit board: 8.46667cm x 5.64444cm
stripboards: 1

parts:
  Part2 = Arduino Nano (Rev3.0)
  U2 = Voltage Regulator - 5V [package="TO220 [THT]"]
  C1 = Ceramic Capacitor [capacitance=100nF package="100 mil [THT, multilayer]"]
  C2 = Ceramic Capacitor [capacitance=100nF package="100 mil [THT, multilayer]"]
  LED1_-_12V = Super Flux LED blue [color=White]
  Q2 = Basic FET N-Channel [package="TO220 [THT]"]
  R2 = Resistor [tolerance=±5% resistance=220 package=THT]
  LED1 = LED - 5mm [color="Red (633nm)" package="5 mm [THT]"]
  R3 = Resistor [tolerance=±5% resistance=220 package=THT]
  S1 = Pushbutton [package="[THT]"]
  R4 = Resistor [tolerance=±5% resistance=220 package=THT]
  S2 = Pushbutton [package="[THT]"]
  R5 = Resistor [tolerance=±5% resistance=220 package=THT]
  S3 = Pushbutton [package="[THT]"]
  R6 = Resistor [tolerance=±5% resistance=220 package=THT]
  LED1_-_12V1 = Super Flux LED blue [color=White]
  Q3 = Basic FET N-Channel [package="TO220 [THT]"]
  R7 = Resistor [tolerance=±5% resistance=220 package=THT]
  LED1_-_12V2 = Super Flux LED blue [color=White]
  Q4 = Basic FET N-Channel [package="TO220 [THT]"]
  R8 = Resistor [tolerance=±5% resistance=220 package=THT]

nets (from the schematic view):
  GND: Part2.GND, U2.GND, C1.0, C2.0, Q2.source, R3.Pin_1, R4.Pin_1, R5.Pin_1, R6.Pin_1, Q3.source, Q4.source
  N1: Part2.D2, R8.Pin_1
  N2: Part2.D3, R7.Pin_1
  N3: Part2.D4, R2.Pin_1
  N4: Part2.D8, S3.Pin_3, S3.Pin_4, R6.Pin_0
  N5: Part2.D9, S2.Pin_3, S2.Pin_4, R5.Pin_0
  N6: Part2.D10, S1.Pin_3, S1.Pin_4, R4.Pin_0
  N7: Part2.VIN, U2.output_voltage, C1.1, LED1.anode, S1.Pin_1, S1.Pin_2, S2.Pin_1, S3.Pin_1, S3.Pin_2
  12V: U2.input_voltage, C2.1, LED1_-_12V.anode, LED1_-_12V1.anode, LED1_-_12V2.anode
  N8: LED1_-_12V.cathode, Q2.drain
  N9: Q2.gate, R2.Pin_0
  N10: LED1.cathode, R3.Pin_0
  N11: Q3.gate, R7.Pin_0
  N12: LED1_-_12V2.cathode, Q4.drain
  N13: Q4.gate, R8.Pin_0
